# Fritzing sketch MAULI_202501 (saved by Fritzing 0.9.6b)
breadboards: 1

parts:
  Pico_H1 = Raspberry Pi Pico H
  HC-SR04_Sensor_1 = HC-SR04 Ultrasonic Distance Sensor
  LCD = LCD1602-I2C

nets:
  N1: Pico_H1.VBUS, LCD.VCC
  GND: Pico_H1.GND, HC-SR04_Sensor_1.GND, LCD.GND
  3V3: Pico_H1.3V3, HC-SR04_Sensor_1.VCC
  N2: Pico_H1.GP17, LCD.SCL
  N3: Pico_H1.GP16, LCD.SDA
  N4: Pico_H1.GP1, HC-SR04_Sensor_1.ECHO
  N5: Pico_H1.GP0, HC-SR04_Sensor_1.TRIG

custom parts:
  Raspberry Pi Pico H: Raspberry Pi Pico H. Based around the RP2040 microcontroller the Pico H is a low cost microcontroller device bringing Raspberry Pi quality, cost, and easy of use to the microcontroller space.
  LCD1602-I2C: A standard character display, usually with 2x16 characters. Comes in many colors with LCM1602 IIC attached.
